# Fritzing sketch nixieBoard (saved by Fritzing 0.9.3b)
circuit board: 20cm x 9cm
breadboards: 2

parts:
  K155ID1-1 = K155ID1 [package="DIP16 [THT]"]
  IN-1-1 = IN-11 [package="DIP (Dual Inline) [THT]"]  # not connected
  R1 = Resistor [tolerance=±5% resistance=15k package=THT]
  U1 = mystery part, 12 pins [chip_label=1361HVPS]
  J1 = shrouded pin header, 40 pins [form="♂ (shrouded male)"]
  Raspberry_Pi_1 = Raspberry Pi Zero  # not connected

nets:
  N1: K155ID1-1.Input_A, J1.pin15, J1.pin26
  N2: R1.Pin_0, R1.Pin_1
  N3: U1.pin1, U1.pin12
  N4: U1.pin2, U1.pin11
  N5: U1.pin3, U1.pin10
  N6: U1.pin4, U1.pin9
  N7: U1.pin5, U1.pin8
  N8: U1.pin6, U1.pin7
  N9: J1.pin1, J1.pin40
  N10: J1.pin2, J1.pin39
  N11: J1.pin3, J1.pin38
  N12: J1.pin4, J1.pin37
  N13: J1.pin5, J1.pin36
  N14: J1.pin6, J1.pin35
  N15: J1.pin7, J1.pin34
  N16: J1.pin8, J1.pin33
  N17: J1.pin9, J1.pin32
  N18: J1.pin10, J1.pin31
  N19: J1.pin11, J1.pin30
  N20: J1.pin12, J1.pin29
  N21: J1.pin13, J1.pin28
  N22: J1.pin14, J1.pin27
  N23: J1.pin16, J1.pin25
  N24: J1.pin17, J1.pin24
  N25: J1.pin18, J1.pin23
  N26: J1.pin19, J1.pin22
  N27: J1.pin20, J1.pin21

custom parts:
  K155ID1: Russian BDC Register (41141 Clone)
  IN-11: An IN-11 bulb mounted With 16 pins on a 300mil dual inline package (DIP) footprint.
